# Fritzing sketch wiring (saved by Fritzing 0.9.4)
breadboards: 1

parts:
  Raspberry_Pi_Zero1 = Raspberry Pi Zero  # not connected
  IC1 = IC, DIP package, 14 pins [chip_label=74AHCT125]
  Part2 = 24 NeoPixel Ring [part_number=1586]
  JACK1 = 2.1mm Barrel Jack with Terminal Block

nets:
  N1: IC1.pin1, IC1.pin7, Part2.GND, JACK1.NEG
  N2: IC1.pin3, Part2.IN
  N3: Part2.VDD, JACK1.POS

custom parts:
  24 NeoPixel Ring: 24 ultra bright smart LED NeoPixels are arranged in a circle with 2.6" (66mm) outer diameter. The rings are 'chainable' - connect the output pin of one to the input pin of another. Use only one microcontroller pin to control as many as you can chain together! Each LED is addressable as the driver chip is inside the LED. Each one has ~18mA constant current drive so the color will be very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
